# Fritzing sketch mando_campo_tiro (saved by Fritzing 0.9.3b)

parts:
  LCD1 = LCD screen
  S1 = Round Pushbutton
  S6 = Toggle Switch [package=THT]
  VCC1 = Battery
  HC-6 = Bluetooth HC-05 Macho
  BUTTON2 = Arcade Button (green)
  BUTTON3 = Arcade Button (red)
  S7 = Round Pushbutton
  S8 = Round Pushbutton
  S9 = Round Pushbutton
  Εξάρτημα2 = Arduino Nano (Rev3.0)
  TP1 = TP4056 [chip_label=TP4056 package="DIP (Dual Inline) [THT]"]
  U1 = LM2596 step down module
  J1 = Piezo Speaker

nets:
  VDD: LCD1.VDD, S6.L2, HC-6.VCC, Εξάρτημα2.5V
  N1: LCD1.V0, Εξάρτημα2.A4
  N2: LCD1.RS, Εξάρτημα2.A5
  GND: S1.leg0, VCC1.-, HC-6.GND, BUTTON2.no_name_yet, BUTTON3.no_name_yet#1, S7.leg0, S8.leg0, S9.leg0, Εξάρτημα2.GND, Εξάρτημα2.D6, TP1.pin5, U1.IN-, U1.OUT-, J1.pin1
  N3: S1.leg1, Εξάρτημα2.D10
  N4: S6.COM, U1.OUT+
  N5: VCC1.+, TP1.pin4, U1.IN+
  N6: HC-6.TXD, Εξάρτημα2.D1/TX, Εξάρτημα2.D11/MOSI
  N7: HC-6.RXD, Εξάρτημα2.D12/MISO
  N8: BUTTON3.no_name_yet#2, Εξάρτημα2.D7
  N9: S7.leg1, Εξάρτημα2.D9
  N10: S8.leg1, Εξάρτημα2.D8
  N11: S9.leg1, Εξάρτημα2.D5
  N12: Εξάρτημα2.D4, J1.pin2

custom parts:
  Battery: Your standard 2x 18650 battery pack (7,4 Volts)
  Arcade Button (green): Adafruit Arcade Button (green)
  Arcade Button (red): Adafruit Arcade Button (red)
  TP4056: A DIP stand-in part for whatever IC you want. With 6 pins on a 300mil dual inline package (DIP) footprint.
  LM2596 step down module: LM2596 DC-DC step down power supply module 3 A.
